// Logisim project 4bitCpu.circ as structural Verilog: 1 circuit, main circuit main
module main (
  input  [3:0] in_1,
  input  [3:0] in_2,
  input  [3:0] in_3,
  input  [7:0] in_4
);

  wire Add, and_1_out, button_2_out, CL, comparator_1_eq, comparator_2_gt, comparator_3_gt, CRamBank,
       CRomBankH, CRomBankL, GetInput, JMP, JMP0, LAR, LDI, LRA, Mode, Move, or_1_out, or_2_out, Sub, Zero;
  wire [3:0] AddOut, controlled_buffer_1_out, multiplexer_2_out, multiplexer_3_out, outA, outB, RamOut,
       register_4_q, SubOut;
  wire [7:0] multiplexer_1_out, rom_1_data;
  wire [7:4] register_3_q;
  wire [11:0] counter_1_q, demultiplexer_1_out1, JMPaddr;

  Register #(.width(4)) register_1 (.D(JMPaddr[3:0]), .en(CRomBankL), .clk(CL), .Q(JMPaddr[7:4]));  // open: clr
  Register #(.width(4)) register_2 (.D(JMPaddr[3:0]), .en(CRomBankH), .clk(CL), .Q(JMPaddr[11:8]));  // open: clr
  Comparator #(.width(4)) comparator_1 (.a(outA), .b(4'b0000), .eq(comparator_1_eq));  // open: gt, lt
  or or_1 (or_1_out, JMP, and_1_out);
  and and_1 (and_1_out, comparator_1_eq, JMP0);
  Clock #(.highDuration(4), .lowDuration(4)) clock_1 (.out(CL));
  Counter #(.max('hfff), .width(12)) counter_1 (
    .load(or_1_out), .up(1'b1), .clk(CL), .D(JMPaddr), .Q(counter_1_q));  // open: clr, count, carry
  Demultiplexer #(.width(12)) demultiplexer_1 (
    .out0({in_2, in_1, in_3}), .out1(demultiplexer_1_out1), .in(counter_1_q), .sel(Mode));
  ROM #(.addrWidth(12)) rom_1 (.addr(demultiplexer_1_out1), .data(rom_1_data));
  Button button_1 ();  // open: out
  Button button_2 (.out(button_2_out));
  Button button_3 ();  // open: out
  Button button_4 ();  // open: out
  Button button_5 ();  // open: out
  Button button_6 ();  // open: out
  Multiplexer #(.width(8)) multiplexer_1 (.in0(in_4), .in1(rom_1_data), .out(multiplexer_1_out), .sel(Mode));
  Register register_3 (.D(multiplexer_1_out), .en(1'b1), .clk(CL), .Q({register_3_q, JMPaddr[3:0]}), .clr(1'b0));
  // DipSwitch #(.number(1)) dipswitch_1: pin names not known; wires that end beside it: Mode
  or or_2 (or_2_out, Sub, LDI, Add, Move, LRA);
  Decoder #(.select(4)) decoder_1 (
    .out0(Zero), .out1(LDI), .out2(Move), .out3(Add), .out4(Sub), .out5(JMP), .out6(JMP0), .out7(CRomBankL),
    .out8(CRomBankH), .out9(CRamBank), .out10(LAR), .out11(LRA), .out12(GetInput), .sel(register_3_q),
    .en(1'b1));  // open: out13, out14, out15
  assign controlled_buffer_1_out = Move ? outB : 4'bz;  // Controlled_Buffer controlled_buffer_1
  Multiplexer #(.width(4)) multiplexer_2 (
    .in0(outB), .in1(JMPaddr[3:0]), .out(multiplexer_2_out), .sel(comparator_2_gt));
  Comparator #(.width(4)) comparator_2 (.a(JMPaddr[3:0]), .b(4'b0000), .gt(comparator_2_gt));  // open: eq, lt
  Multiplexer #(.width(4)) multiplexer_3 (
    .in0(outB), .in1(JMPaddr[3:0]), .out(multiplexer_3_out), .sel(comparator_3_gt));
  Comparator #(.width(4)) comparator_3 (.a(JMPaddr[3:0]), .b(4'b0000), .gt(comparator_3_gt));  // open: eq, lt
  assign controlled_buffer_1_out = LRA ? RamOut : 4'bz;  // Controlled_Buffer controlled_buffer_2
  assign controlled_buffer_1_out = LDI ? JMPaddr[3:0] : 4'bz;  // Controlled_Buffer controlled_buffer_3
  assign controlled_buffer_1_out = Add ? AddOut : 4'bz;  // Controlled_Buffer controlled_buffer_4
  assign controlled_buffer_1_out = Sub ? AddOut : 4'bz;  // Controlled_Buffer controlled_buffer_5
  Adder #(.width(4)) adder_1 (.a(outA), .b(multiplexer_2_out), .out(AddOut));  // open: cin, cout
  Subtractor #(.width(4)) subtractor_1 (.a(outA), .b(multiplexer_3_out), .out(SubOut));  // open: bin, bout
  Register #(.width(4)) register_4 (.D(JMPaddr[3:0]), .en(CRamBank), .clk(CL), .Q(register_4_q));  // open: clr
  Register #(.width(4)) A (.D(controlled_buffer_1_out), .en(or_2_out), .clk(CL), .Q(outA));  // open: clr
  Register #(.width(4)) B (.D(outA), .en(Move), .clk(CL), .Q(outB));  // open: clr
  RAM #(.dataWidth(4)) ram_1 (
    .addr({register_4_q, JMPaddr[3:0]}), .we(LAR), .oe(LRA), .clk(CL), .din(outA), .dout(RamOut));

  // Other names for the same wires on the sheet: Operand[3:0] = JMPaddr[3:0]

  // Notes on the sheet:
  //   JMP Loading
  //   contents of rom_1 (hex, n*v repeats v):
  //   0 a0 7*0 a0 0 0 0 a0 0 0 a0
  //   4
  //   1
  //   2
  //   3
  //   5
  //   6
  //   Opcode
  //   Logism/FPGA Mode
  //   ALU
  //   General Registers
  //   RAM
endmodule
